# Fritzing sketch filtro_ar (saved by Fritzing 0.9.3b)
breadboards: 1

parts:
  ADC1 = MCP3008 [package=dil16]
  Raspberry_Pi_1 = Raspberry Pi 3 [part_number=RPI-3-V1.2]
  U2 = LCD-16X2 [package=lcd-16x2]
  U3 = POT_SWITCH [package=pot_pth]
  U4 = POT_SWITCH [package=pot_pth]

nets:
  N1: ADC1.CH0, U3.G$2_1
  N2: ADC1.CH1, U4.G$2_1
  GND: ADC1.DGND, ADC1.AGND, Raspberry_Pi_1.GND, U2.VSS, U2.R_W, U2.K, U3.G$1_E, U4.G$1_E
  N3: ADC1.CS/SHDN, Raspberry_Pi_1.GPIO22
  N4: ADC1.Din, Raspberry_Pi_1.GPIO24
  N5: ADC1.Dout, Raspberry_Pi_1.GPIO23
  N6: ADC1.CLK, Raspberry_Pi_1.GPIO18
  VDD: ADC1.VREF, ADC1.VDD, Raspberry_Pi_1.5V, U2.VDD, U2.VO, U2.A, U3.G$1_A, U4.G$1_A
  N7: Raspberry_Pi_1.GPIO13, U2.DB7
  N8: Raspberry_Pi_1.GPIO19, U2.DB4
  N9: Raspberry_Pi_1.GPIO21, U2.DB6
  N10: Raspberry_Pi_1.GPIO20, U2.E
  N11: Raspberry_Pi_1.GPIO16, U2.DB5
  N12: Raspberry_Pi_1.GPIO25, U2.RS

notes:
  Pinos fisicos nao estao na ordem tradicional.
  A ordem e:
  01 - em cima a direita
  20 - em cima a esquerda
  21 - embaixo a esquerda
  40 - embaixo a direita
  1
  40
  20
  21
